// Digital circuit ALU.dig as structural Verilog
module ALU (
  input  [7:0] A,
  input  [7:0] B,
  input  clk,
  input  [2:0] Selector,
  input  Acumulador,
  output [7:0] out_6
);

  wire [7:0] A_t, Adder, B_t, DIV, MULT, multiplexer_1_out, multiplexer_2_out, Sf, Sub, XOR;

  Multiplexer #(.Bits(8)) multiplexer_1 (.sel(Acumulador), .in_0(B), .in_1(out_6), .out(multiplexer_1_out));
  Registrador8bits u_A (.D(A), .CLK(clk), .S(A_t));
  Registrador8bits u_B (.D(multiplexer_1_out), .CLK(clk), .S(B_t));
  Adder8bits adder8bits_1 (.B(B_t), .cIn(1'b0), .A(A_t), .S(Adder));  // open: cOut
  Divisor8bits divisor8bits_1 (.A(A_t), .B(B_t), .S(DIV));
  // LeftShift leftshift_1: pin names not known; wires that end beside it: A_t, Sf
  Subtrator8bits subtrator8bits_1 (.B(B_t), .A(A_t), .S(Sub));  // open: cOut
  Multiplicador8bits multiplicador8bits_1 (.B(B_t), .A(A_t), ._1(MULT));  // open: _2
  XOR8bits xor8bits_1 (.A(A_t), .B(B_t), .S(XOR));
  Multiplexer #(.Bits(8), .Selector_Bits(3)) multiplexer_2 (
    .sel(Selector), .in_0(Adder), .in_1(DIV), .in_2(Sf), .in_3(Sub), .in_4(MULT), .in_5(XOR), .in_6(XOR),
    .in_7(XOR), .out(multiplexer_2_out));
  Registrador8bits registrador8bits_1 (.D(multiplexer_2_out), .CLK(clk), .S(out_6));

  // Other names for the same wires on the sheet: Ac = Acumulador; S[7:0] = out_6; Selec[2:0] = Selector
endmodule
