// Digital circuit Adder16bits.dig as structural Verilog
module Adder16bits (
  input  [15:0] B,
  input  cIn,
  input  [15:0] A,
  output [15:0] S,
  output cOut
);

  wire adder_1bit_1_cout, adder_1bit_2_cout, adder_1bit_3_cout, adder_1bit_4_cout, adder_1bit_5_cout,
       adder_1bit_6_cout, adder_1bit_7_cout, adder_1bit_8_cout, adder_1bit_9_cout, adder_1bit_10_cout,
       adder_1bit_11_cout, adder_1bit_12_cout, adder_1bit_13_cout, adder_1bit_14_cout, adder_1bit_15_cout;

  Adder_1bit adder_1bit_1 (.A(A[0]), .B(B[0]), .cIN(cIn), .S(S[0]), .cOut(adder_1bit_1_cout));
  Adder_1bit adder_1bit_2 (.A(A[1]), .B(B[1]), .cIN(adder_1bit_1_cout), .S(S[1]), .cOut(adder_1bit_2_cout));
  Adder_1bit adder_1bit_3 (.A(A[2]), .B(B[2]), .cIN(adder_1bit_2_cout), .S(S[2]), .cOut(adder_1bit_3_cout));
  Adder_1bit adder_1bit_4 (.A(A[3]), .B(B[3]), .cIN(adder_1bit_3_cout), .S(S[3]), .cOut(adder_1bit_4_cout));
  Adder_1bit adder_1bit_5 (.A(A[4]), .B(B[4]), .cIN(adder_1bit_4_cout), .S(S[4]), .cOut(adder_1bit_5_cout));
  Adder_1bit adder_1bit_6 (.A(A[5]), .B(B[5]), .cIN(adder_1bit_5_cout), .S(S[5]), .cOut(adder_1bit_6_cout));
  Adder_1bit adder_1bit_7 (.A(A[6]), .B(B[6]), .cIN(adder_1bit_6_cout), .S(S[6]), .cOut(adder_1bit_7_cout));
  Adder_1bit adder_1bit_8 (.A(A[7]), .B(B[7]), .cIN(adder_1bit_7_cout), .S(S[7]), .cOut(adder_1bit_8_cout));
  Adder_1bit adder_1bit_9 (.A(A[8]), .B(B[8]), .cIN(adder_1bit_8_cout), .S(S[8]), .cOut(adder_1bit_9_cout));
  Adder_1bit adder_1bit_10 (.A(A[9]), .B(B[9]), .cIN(adder_1bit_9_cout), .S(S[9]), .cOut(adder_1bit_10_cout));
  Adder_1bit adder_1bit_11 (.A(A[10]), .B(B[10]), .cIN(adder_1bit_10_cout), .S(S[10]), .cOut(adder_1bit_11_cout));
  Adder_1bit adder_1bit_12 (.A(A[11]), .B(B[11]), .cIN(adder_1bit_11_cout), .S(S[11]), .cOut(adder_1bit_12_cout));
  Adder_1bit adder_1bit_13 (.A(A[12]), .B(B[12]), .cIN(adder_1bit_12_cout), .S(S[12]), .cOut(adder_1bit_13_cout));
  Adder_1bit adder_1bit_14 (.A(A[13]), .B(B[13]), .cIN(adder_1bit_13_cout), .S(S[13]), .cOut(adder_1bit_14_cout));
  Adder_1bit adder_1bit_15 (.A(A[14]), .B(B[14]), .cIN(adder_1bit_14_cout), .S(S[14]), .cOut(adder_1bit_15_cout));
  Adder_1bit adder_1bit_16 (.A(A[15]), .B(B[15]), .cIN(adder_1bit_15_cout), .S(S[15]), .cOut(cOut));

  // Other names for the same wires on the sheet: A1 = A[0]; A2 = A[1]; A3 = A[2]; A4 = A[3]; A5 = A[4]; A6 = A[5];
  //   A7 = A[6]; A8 = A[7]; A9 = A[8]; A10 = A[9]; A11 = A[10]; A12 = A[11]; A13 = A[12]; A14 = A[13]; A15 = A[14];
  //   A16 = A[15]; B1 = B[0]; B2 = B[1]; B3 = B[2]; B4 = B[3]; B5 = B[4]; B6 = B[5]; B7 = B[6]; B8 = B[7]; B9 = B[8];
  //   B10 = B[9]; B11 = B[10]; B12 = B[11]; B13 = B[12]; B14 = B[13]; B15 = B[14]; B16 = B[15]
endmodule
