// Digital circuit Adder8bits.dig as structural Verilog
module Adder8bits (
  input  [7:0] B,
  input  cIn,
  input  [7:0] A,
  output [7:0] S,
  output cOut
);

  wire adder_1bit_1_cout, adder_1bit_2_cout, adder_1bit_3_cout, adder_1bit_4_cout, adder_1bit_5_cout,
       adder_1bit_6_cout, adder_1bit_7_cout;

  Adder_1bit adder_1bit_1 (.A(A[0]), .B(B[0]), .cIN(cIn), .S(S[0]), .cOut(adder_1bit_1_cout));
  Adder_1bit adder_1bit_2 (.A(A[1]), .B(B[1]), .cIN(adder_1bit_1_cout), .S(S[1]), .cOut(adder_1bit_2_cout));
  Adder_1bit adder_1bit_3 (.A(A[2]), .B(B[2]), .cIN(adder_1bit_2_cout), .S(S[2]), .cOut(adder_1bit_3_cout));
  Adder_1bit adder_1bit_4 (.A(A[3]), .B(B[3]), .cIN(adder_1bit_3_cout), .S(S[3]), .cOut(adder_1bit_4_cout));
  Adder_1bit adder_1bit_5 (.A(A[4]), .B(B[4]), .cIN(adder_1bit_4_cout), .S(S[4]), .cOut(adder_1bit_5_cout));
  Adder_1bit adder_1bit_6 (.A(A[5]), .B(B[5]), .cIN(adder_1bit_5_cout), .S(S[5]), .cOut(adder_1bit_6_cout));
  Adder_1bit adder_1bit_7 (.A(A[6]), .B(B[6]), .cIN(adder_1bit_6_cout), .S(S[6]), .cOut(adder_1bit_7_cout));
  Adder_1bit adder_1bit_8 (.A(A[7]), .B(B[7]), .cIN(adder_1bit_7_cout), .S(S[7]), .cOut(cOut));

  // Other names for the same wires on the sheet: A1 = A[0]; A2 = A[1]; A3 = A[2]; A4 = A[3]; A5 = A[4]; A6 = A[5];
  //   A7 = A[6]; A8 = A[7]; B1 = B[0]; B2 = B[1]; B3 = B[2]; B4 = B[3]; B5 = B[4]; B6 = B[5]; B7 = B[6]; B8 = B[7]
endmodule
