// Digital circuit Adder_1bit.dig as structural Verilog
module Adder_1bit (
  input  A,
  input  B,
  input  cIN,
  output S,
  output cOut
);

  wire and_1_out, and_2_out, and_3_out;

  xor xor_1 (S, A, B, cIN);
  and and_1 (and_1_out, A, B);
  and and_2 (and_2_out, B, cIN);
  and and_3 (and_3_out, A, cIN);
  or or_1 (cOut, and_1_out, and_2_out, and_3_out);
endmodule
