// Digital circuit Divisor 8bits.dig as structural Verilog
module Divisor_8bits (
  input  [7:0] A,
  input  [7:0] B
);

  wire adder_1bit_1_cout, adder_1bit_2_cout, adder_1bit_3_cout, adder_1bit_4_cout, adder_1bit_5_cout,
       adder_1bit_6_cout, adder_1bit_7_cout, R1, R2, R3, R4, R5, R6, R7, S1, S2, S3, S4, S5, S6, S7, S8;

  Divisor1bit divisor1bit_1 (.B(B[0]), .A(A[0]), .S(S1));
  Divisor1bit divisor1bit_2 (.B(B[1]), .A(A[1]), .S(S2));
  Divisor1bit divisor1bit_3 (.B(B[2]), .A(A[2]), .S(S3));
  Divisor1bit divisor1bit_4 (.B(B[3]), .A(A[3]), .S(S4));
  Divisor1bit divisor1bit_5 (.B(B[4]), .A(A[4]), .S(S5));
  Divisor1bit divisor1bit_6 (.B(B[5]), .A(A[5]), .S(S6));
  Divisor1bit divisor1bit_7 (.B(B[6]), .A(A[6]), .S(S7));
  Divisor1bit divisor1bit_8 (.B(B[7]), .A(A[7]), .S(S8));
  Adder_1bit adder_1bit_1 (.A(1'b0), .B(S1), .cIN(1'b0), .S(R1), .cOut(adder_1bit_1_cout));
  Adder_1bit adder_1bit_2 (.A(R1), .B(S2), .cIN(adder_1bit_1_cout), .S(R2), .cOut(adder_1bit_2_cout));
  Adder_1bit adder_1bit_3 (.B(S3), .cIN(adder_1bit_2_cout), .S(R3), .cOut(adder_1bit_3_cout));  // open: A
  Adder_1bit adder_1bit_4 (.B(S4), .cIN(adder_1bit_3_cout), .S(R4), .cOut(adder_1bit_4_cout));  // open: A
  Adder_1bit adder_1bit_5 (.B(S5), .cIN(adder_1bit_4_cout), .S(R5), .cOut(adder_1bit_5_cout));  // open: A
  Adder_1bit adder_1bit_6 (.B(S6), .cIN(adder_1bit_5_cout), .S(R6), .cOut(adder_1bit_6_cout));  // open: A
  Adder_1bit adder_1bit_7 (.B(S7), .cIN(adder_1bit_6_cout), .S(R7), .cOut(adder_1bit_7_cout));  // open: A
  // Pins of 1 and 8 bits meet at A
  // Pins of 1 and 8 bits meet at B

  // Other names for the same wires on the sheet: A1 = A[0]; A2 = A[1]; A3 = A[2]; A4 = A[3]; A5 = A[4]; A6 = A[5];
  //   A7 = A[6]; A8 = A[7]; B1 = B[0]; B2 = B[1]; B3 = B[2]; B4 = B[3]; B5 = B[4]; B6 = B[5]; B7 = B[6]; B8 = B[7]
endmodule
