// Digital circuit Divisor8bits.dig as structural Verilog
module Divisor8bits (
  input  [7:0] A,
  input  [7:0] B,
  output [7:0] S
);

  wire S2, S3, S4, S5, S6, S7, S8, SF1, SF2, SF3, SF4, SF5, SF6, SF7;
  wire [7:0] S1;

  divisorSimples divisorsimples_1 (.A({A[7], {7{1'b0}}}), .B(B), .S(S1), .cOut(S[7]));
  // divisorSimples divisorsimples_2: pin names not known; wires that end beside it: SF1, B, S2, S[6]
  // divisorSimples divisorsimples_3: pin names not known; wires that end beside it: SF2, B, S3, S[5]
  // divisorSimples divisorsimples_4: pin names not known; wires that end beside it: SF3, B, S4, S[4]
  // divisorSimples divisorsimples_5: pin names not known; wires that end beside it: SF4, B, S5, S[3]
  // divisorSimples divisorsimples_6: pin names not known; wires that end beside it: SF5, B, S6, S[2]
  // divisorSimples divisorsimples_7: pin names not known; wires that end beside it: SF6, B, S7, S[1]
  // divisorSimples divisorsimples_8: pin names not known; wires that end beside it: SF7, B, S8, S[0]
  // LeftShiftG leftshiftg_1: pin names not known; wires that end beside it: S1, A[6], SF1
  // LeftShiftG leftshiftg_2: pin names not known; wires that end beside it: S2, A[5], SF2
  // LeftShiftG leftshiftg_3: pin names not known; wires that end beside it: S3, A[4], SF3
  // LeftShiftG leftshiftg_4: pin names not known; wires that end beside it: S4, A[3], SF4
  // LeftShiftG leftshiftg_5: pin names not known; wires that end beside it: S5, A[2], SF5
  // LeftShiftG leftshiftg_6: pin names not known; wires that end beside it: S6, A[1], SF6
  // LeftShiftG leftshiftg_7: pin names not known; wires that end beside it: S7, A[0], SF7

  // Other names for the same wires on the sheet: A1 = A[0]; A2 = A[1]; A3 = A[2]; A4 = A[3]; A5 = A[4]; A6 = A[5];
  //   A7 = A[6]; A8 = A[7]; ex[7] = A[7]; C1 = S[7]; C2 = S[6]; C3 = S[5]; C4 = S[4]; C5 = S[3]; C6 = S[2]; C7 = S[1];
  //   C8 = S[0]
endmodule
