// Digital circuit LeftShift.dig as structural Verilog
module LeftShift (
  input  [7:0] A,
  output [15:0] S
);

  // Pins of 8 and 16 bits meet at {S[15:8], A[6:0], 1'b0}

  assign S[7:0] = {A[6:0], 1'b0};
endmodule
