// Digital circuit LeftShift16bits.dig as structural Verilog
module LeftShift16bits (
  input  [15:0] A,
  output [15:0] S
);

  // Pins of 8 and 16 bits meet at A

  assign S = {A[14:0], 1'b0};
endmodule
