// Digital circuit LeftShiftCout.dig as structural Verilog
module LeftShiftCout (
  input  [7:0] A,
  output [15:0] S,
  output [15:0] cOut
);

  // Pins of 8 and 16 bits meet at {S[15:8], A[6:0], 1'b0}
  // Pins of 1 and 16 bits meet at {cOut[15:1], A[7]}

  assign cOut[0] = A[7];
  assign S[7:0] = {A[6:0], 1'b0};
endmodule
