// Digital circuit LeftShiftG.dig as structural Verilog
module LeftShiftG (
  input  [7:0] E,
  input  IN,
  output [7:0] S
);

  // Pins of 1 and 8 bits meet at {E[6:0], IN}

  assign S = {E[6:0], IN};
endmodule
