// Digital circuit Multiplicador1x4.dig as structural Verilog
module Multiplicador1x4 (
  input  A,
  input  [3:0] B,
  output [3:0] S
);

  Multiplicador1bit multiplicador1bit_1 (.A(A), .B(B[0]), .S(S[0]));
  Multiplicador1bit multiplicador1bit_2 (.A(A), .B(B[1]), .S(S[1]));
  Multiplicador1bit multiplicador1bit_3 (.A(A), .B(B[2]), .S(S[2]));
  Multiplicador1bit multiplicador1bit_4 (.A(A), .B(B[3]), .S(S[3]));

  // Other names for the same wires on the sheet: A1 = A; B1 = B[0]; B2 = B[1]; B3 = B[2]; B4 = B[3]; S1 = S[0];
  //   S2 = S[1]; S3 = S[2]; S4 = S[3]
endmodule
