// Digital circuit Multiplicador1x8.dig as structural Verilog
module Multiplicador1x8 (
  input  A,
  input  [7:0] B,
  output [7:0] S
);

  Multiplicador1bit multiplicador1bit_1 (.A(A), .B(B[0]), .S(S[0]));
  Multiplicador1bit multiplicador1bit_2 (.A(A), .B(B[1]), .S(S[1]));
  Multiplicador1bit multiplicador1bit_3 (.A(A), .B(B[2]), .S(S[2]));
  Multiplicador1bit multiplicador1bit_4 (.A(A), .B(B[3]), .S(S[3]));
  Multiplicador1bit multiplicador1bit_5 (.A(A), .B(B[4]), .S(S[4]));
  Multiplicador1bit multiplicador1bit_6 (.A(A), .B(B[5]), .S(S[5]));
  Multiplicador1bit multiplicador1bit_7 (.A(A), .B(B[6]), .S(S[6]));
  Multiplicador1bit multiplicador1bit_8 (.A(A), .B(B[7]), .S(S[7]));
  // Pins of 4 and 8 bits meet at B

  // Other names for the same wires on the sheet: A1 = A; B1 = B[0]; B2 = B[1]; B3 = B[2]; B4 = B[3]; B5 = B[4];
  //   B6 = B[5]; B7 = B[6]; B8 = B[7]; S1 = S[0]; S2 = S[1]; S3 = S[2]; S4 = S[3]; S5 = S[4]; S6 = S[5]; S7 = S[6];
  //   S8 = S[7]
endmodule
