// Digital circuit Multiplicador2x2.dig as structural Verilog
module Multiplicador2x2 (
  input  [1:0] A,
  input  [1:0] B,
  output [3:0] S
);

  wire adder_1bit_1_cout, adder_1bit_2_cout, S1, S2, S3, S4;

  Multiplicador1bit multiplicador1bit_1 (.A(A[0]), .B(B[0]), .S(S1));
  Multiplicador1bit multiplicador1bit_2 (.A(A[0]), .B(B[1]), .S(S2));
  Multiplicador1bit multiplicador1bit_3 (.A(A[1]), .B(B[0]), .S(S3));
  Multiplicador1bit multiplicador1bit_4 (.A(A[1]), .B(B[1]), .S(S4));
  Adder_1bit adder_1bit_1 (.A(1'b0), .B(S1), .cIN(1'b0), .S(S[0]), .cOut(adder_1bit_1_cout));
  Adder_1bit adder_1bit_2 (.A(S3), .B(S2), .cIN(adder_1bit_1_cout), .S(S[1]), .cOut(adder_1bit_2_cout));
  Adder_1bit adder_1bit_3 (.A(1'b0), .B(S4), .cIN(adder_1bit_2_cout), .S(S[2]), .cOut(S[3]));

  // Other names for the same wires on the sheet: A1 = A[0]; A2 = A[1]; B1 = B[0]; B2 = B[1]
endmodule
