// Digital circuit Multiplicador8bits.dig as structural Verilog
module Multiplicador8bits (
  input  [7:0] B,
  input  [7:0] A,
  output [15:0] _1,
  output [15:0] _2
);

  wire adder16bits_1_cout, adder16bits_2_cout, adder16bits_3_cout, adder16bits_4_cout, adder16bits_5_cout,
       adder16bits_6_cout, bitextender8x16_2_p2, bitextender8x16_3_p2, bitextender8x16_4_p2,
       bitextender8x16_5_p2, bitextender8x16_6_p2, bitextender8x16_7_p2, bitextender8x16_8_p2,
       leftshift16bits_2_p2, leftshift16bits_3_p2, leftshift16bits_4_p2, leftshift16bits_5_p2,
       leftshift16bits_6_p2, leftshift16bits_7_p2, leftshift16bits_9_p2, leftshift16bits_10_p2,
       leftshift16bits_11_p2, leftshift16bits_12_p2, leftshift16bits_13_p2, leftshift16bits_15_p2,
       leftshift16bits_16_p2, leftshift16bits_17_p2, leftshift16bits_18_p2, leftshift16bits_20_p2,
       leftshift16bits_21_p2, leftshift16bits_22_p2, leftshift16bits_24_p2, leftshift16bits_25_p2,
       leftshift16bits_27_p2, leftshift16bits_28_p2, multiplicador1x8_2_p3, multiplicador1x8_3_p3,
       multiplicador1x8_4_p3, multiplicador1x8_5_p3, multiplicador1x8_6_p3, multiplicador1x8_7_p3,
       multiplicador1x8_8_p3;
  wire [7:0] multiplicador1x8_1_p3;
  wire [15:0] adder16bits_1_s, adder16bits_2_s, adder16bits_3_s, adder16bits_4_s, adder16bits_5_s,
       adder16bits_6_s, bitextender8x16_1_s, leftshift16bits_1_p2, leftshift16bits_8_p2,
       leftshift16bits_14_p2, leftshift16bits_19_p2, leftshift16bits_23_p2, leftshift16bits_26_p2;

  // Multiplicador1x8 multiplicador1x8_1: pin names not known; wires that end beside it: A[0], B, multiplicador1x8_1_p3
  // Multiplicador1x8 multiplicador1x8_2: pin names not known; wires that end beside it: A[1], B, multiplicador1x8_2_p3
  // Multiplicador1x8 multiplicador1x8_3: pin names not known; wires that end beside it: A[2], B, multiplicador1x8_3_p3
  // Multiplicador1x8 multiplicador1x8_4: pin names not known; wires that end beside it: A[3], B, multiplicador1x8_4_p3
  // Multiplicador1x8 multiplicador1x8_5: pin names not known; wires that end beside it: A[4], B, multiplicador1x8_5_p3
  // Multiplicador1x8 multiplicador1x8_6: pin names not known; wires that end beside it: A[5], B, multiplicador1x8_6_p3
  // Multiplicador1x8 multiplicador1x8_7: pin names not known; wires that end beside it: A[6], B, multiplicador1x8_7_p3
  // Multiplicador1x8 multiplicador1x8_8: pin names not known; wires that end beside it: A[7], B, multiplicador1x8_8_p3
  BitExtender8x16 bitextender8x16_1 (.A(multiplicador1x8_1_p3), .S(bitextender8x16_1_s));
  // BitExtender8x16 bitextender8x16_2: pin names not known; wires that end beside it: multiplicador1x8_2_p3, bitextender8x16_2_p2
  // BitExtender8x16 bitextender8x16_3: pin names not known; wires that end beside it: multiplicador1x8_3_p3, bitextender8x16_3_p2
  // BitExtender8x16 bitextender8x16_4: pin names not known; wires that end beside it: multiplicador1x8_4_p3, bitextender8x16_4_p2
  // BitExtender8x16 bitextender8x16_5: pin names not known; wires that end beside it: multiplicador1x8_5_p3, bitextender8x16_5_p2
  // BitExtender8x16 bitextender8x16_6: pin names not known; wires that end beside it: multiplicador1x8_6_p3, bitextender8x16_6_p2
  // BitExtender8x16 bitextender8x16_7: pin names not known; wires that end beside it: multiplicador1x8_7_p3, bitextender8x16_7_p2
  // BitExtender8x16 bitextender8x16_8: pin names not known; wires that end beside it: multiplicador1x8_8_p3, bitextender8x16_8_p2
  // LeftShift16bits leftshift16bits_1: pin names not known; wires that end beside it: bitextender8x16_2_p2, leftshift16bits_1_p2
  // LeftShift16bits leftshift16bits_2: pin names not known; wires that end beside it: bitextender8x16_3_p2, leftshift16bits_2_p2
  // LeftShift16bits leftshift16bits_3: pin names not known; wires that end beside it: bitextender8x16_4_p2, leftshift16bits_3_p2
  // LeftShift16bits leftshift16bits_4: pin names not known; wires that end beside it: bitextender8x16_5_p2, leftshift16bits_4_p2
  // LeftShift16bits leftshift16bits_5: pin names not known; wires that end beside it: bitextender8x16_6_p2, leftshift16bits_5_p2
  // LeftShift16bits leftshift16bits_6: pin names not known; wires that end beside it: bitextender8x16_7_p2, leftshift16bits_6_p2
  // LeftShift16bits leftshift16bits_7: pin names not known; wires that end beside it: bitextender8x16_8_p2, leftshift16bits_7_p2
  Adder16bits adder16bits_1 (
    .B(leftshift16bits_1_p2), .cIn(1'b0), .A(bitextender8x16_1_s), .S(adder16bits_1_s),
    .cOut(adder16bits_1_cout));
  // LeftShift16bits leftshift16bits_8: pin names not known; wires that end beside it: leftshift16bits_2_p2, leftshift16bits_8_p2
  // LeftShift16bits leftshift16bits_9: pin names not known; wires that end beside it: leftshift16bits_3_p2, leftshift16bits_9_p2
  // LeftShift16bits leftshift16bits_10: pin names not known; wires that end beside it: leftshift16bits_4_p2, leftshift16bits_10_p2
  // LeftShift16bits leftshift16bits_11: pin names not known; wires that end beside it: leftshift16bits_5_p2, leftshift16bits_11_p2
  // LeftShift16bits leftshift16bits_12: pin names not known; wires that end beside it: leftshift16bits_6_p2, leftshift16bits_12_p2
  // LeftShift16bits leftshift16bits_13: pin names not known; wires that end beside it: leftshift16bits_7_p2, leftshift16bits_13_p2
  // LeftShift16bits leftshift16bits_14: pin names not known; wires that end beside it: leftshift16bits_9_p2, leftshift16bits_14_p2
  // LeftShift16bits leftshift16bits_15: pin names not known; wires that end beside it: leftshift16bits_10_p2, leftshift16bits_15_p2
  // LeftShift16bits leftshift16bits_16: pin names not known; wires that end beside it: leftshift16bits_11_p2, leftshift16bits_16_p2
  // LeftShift16bits leftshift16bits_17: pin names not known; wires that end beside it: leftshift16bits_12_p2, leftshift16bits_17_p2
  // LeftShift16bits leftshift16bits_18: pin names not known; wires that end beside it: leftshift16bits_13_p2, leftshift16bits_18_p2
  Adder16bits adder16bits_2 (
    .B(leftshift16bits_8_p2), .cIn(adder16bits_1_cout), .A(adder16bits_1_s), .S(adder16bits_2_s),
    .cOut(adder16bits_2_cout));
  // LeftShift16bits leftshift16bits_19: pin names not known; wires that end beside it: leftshift16bits_15_p2, leftshift16bits_19_p2
  // LeftShift16bits leftshift16bits_20: pin names not known; wires that end beside it: leftshift16bits_16_p2, leftshift16bits_20_p2
  // LeftShift16bits leftshift16bits_21: pin names not known; wires that end beside it: leftshift16bits_17_p2, leftshift16bits_21_p2
  // LeftShift16bits leftshift16bits_22: pin names not known; wires that end beside it: leftshift16bits_18_p2, leftshift16bits_22_p2
  // LeftShift16bits leftshift16bits_23: pin names not known; wires that end beside it: leftshift16bits_20_p2, leftshift16bits_23_p2
  // LeftShift16bits leftshift16bits_24: pin names not known; wires that end beside it: leftshift16bits_21_p2, leftshift16bits_24_p2
  // LeftShift16bits leftshift16bits_25: pin names not known; wires that end beside it: leftshift16bits_22_p2, leftshift16bits_25_p2
  Adder16bits adder16bits_3 (
    .B(leftshift16bits_14_p2), .cIn(adder16bits_2_cout), .A(adder16bits_2_s), .S(adder16bits_3_s),
    .cOut(adder16bits_3_cout));
  // LeftShift16bits leftshift16bits_26: pin names not known; wires that end beside it: leftshift16bits_24_p2, leftshift16bits_26_p2
  // LeftShift16bits leftshift16bits_27: pin names not known; wires that end beside it: leftshift16bits_25_p2, leftshift16bits_27_p2
  // LeftShift16bits leftshift16bits_28: pin names not known; wires that end beside it: leftshift16bits_27_p2, leftshift16bits_28_p2
  Adder16bits adder16bits_4 (
    .B(leftshift16bits_26_p2), .cIn(adder16bits_6_cout), .A(adder16bits_6_s), .S(adder16bits_4_s),
    .cOut(adder16bits_4_cout));
  Adder16bits adder16bits_5 (
    .B(leftshift16bits_19_p2), .cIn(adder16bits_3_cout), .A(adder16bits_3_s), .S(adder16bits_5_s),
    .cOut(adder16bits_5_cout));
  Adder16bits adder16bits_6 (
    .B(leftshift16bits_23_p2), .cIn(adder16bits_5_cout), .A(adder16bits_5_s), .S(adder16bits_6_s),
    .cOut(adder16bits_6_cout));
  // Adder16bits adder16bits_7: pin names not known; wires that end beside it: leftshift16bits_28_p2, adder16bits_4_cout, adder16bits_4_s, _1[7:0]
  // Pins of 8 and 16 bits meet at _1
  // Pins of 8 and 16 bits meet at _2
endmodule
