// Digital circuit Registrador1bit.dig as structural Verilog
module Registrador1bit (
  input  D,
  input  CLK,
  output S
);

  wire nand_1_out, nand_2_out, nand_4_out, not_1_out;

  not not_1 (not_1_out, D);
  nand nand_1 (nand_1_out, D, CLK);
  nand nand_2 (nand_2_out, not_1_out, CLK);
  nand nand_3 (S, nand_1_out, nand_4_out);
  nand nand_4 (nand_4_out, S, nand_2_out);
endmodule
