// Digital circuit Registrador8bits.dig as structural Verilog
module Registrador8bits (
  input  [7:0] D,
  input  CLK,
  output [7:0] S
);

  Registrador1bit registrador1bit_1 (.D(D[0]), .CLK(CLK), .S(S[0]));
  Registrador1bit registrador1bit_2 (.D(D[1]), .CLK(CLK), .S(S[1]));
  Registrador1bit registrador1bit_3 (.D(D[2]), .CLK(CLK), .S(S[2]));
  Registrador1bit registrador1bit_4 (.D(D[3]), .CLK(CLK), .S(S[3]));
  Registrador1bit registrador1bit_5 (.D(D[4]), .CLK(CLK), .S(S[4]));
  Registrador1bit registrador1bit_6 (.D(D[5]), .CLK(CLK), .S(S[5]));
  Registrador1bit registrador1bit_7 (.D(D[6]), .CLK(CLK), .S(S[6]));
  Registrador1bit registrador1bit_8 (.D(D[7]), .CLK(CLK), .S(S[7]));

  // Other names for the same wires on the sheet: D1 = D[0]; D2 = D[1]; D3 = D[2]; D4 = D[3]; D5 = D[4]; D6 = D[5];
  //   D7 = D[6]; D8 = D[7]; S1 = S[0]; S2 = S[1]; S3 = S[2]; S4 = S[3]; S5 = S[4]; S6 = S[5]; S7 = S[6]; S8 = S[7]
endmodule
