// Digital circuit Somador de 8bits.dig as structural Verilog
module Somador_de_8bits (
  input  in_1,
  input  in_2,
  input  in_3,
  input  in_4,
  input  in_5,
  input  in_6,
  input  in_7,
  input  in_8,
  input  in_9,
  input  in_10,
  input  in_11,
  input  in_12,
  input  in_13,
  input  in_14,
  input  in_15,
  input  in_16,
  input  in_25,
  output out_17,
  output out_18,
  output out_19,
  output out_20,
  output out_21,
  output out_22,
  output out_23,
  output out_24
);

  wire add_1_c_o, add_2_c_o, add_3_c_o, add_4_c_o, add_5_c_o, add_6_c_o, add_7_c_o;

  Add add_1 (.a(in_16), .b(in_8), .c_i(in_25), .s(out_17), .c_o(add_1_c_o));
  Add add_2 (.a(in_15), .b(in_7), .c_i(add_1_c_o), .s(out_18), .c_o(add_2_c_o));
  Add add_3 (.a(in_14), .b(in_6), .c_i(add_2_c_o), .s(out_19), .c_o(add_3_c_o));
  Add add_4 (.a(in_13), .b(in_5), .c_i(add_3_c_o), .s(out_20), .c_o(add_4_c_o));
  Add add_5 (.a(in_12), .b(in_4), .c_i(add_4_c_o), .s(out_21), .c_o(add_5_c_o));
  Add add_6 (.a(in_11), .b(in_3), .c_i(add_5_c_o), .s(out_22), .c_o(add_6_c_o));
  Add add_7 (.a(in_10), .b(in_2), .c_i(add_6_c_o), .s(out_23), .c_o(add_7_c_o));
  Add add_8 (.a(in_9), .b(in_1), .c_i(add_7_c_o), .s(out_24));  // open: c_o
  SixteenSeg sixteenseg_1 ();  // open: led, dp
endmodule
