// Digital circuit Somador.dig as structural Verilog
module Somador (
  input  A,
  input  B,
  input  cIn,
  output S,
  output cOut
);

  wire and_1_out, and_2_out, xor_1_out;

  xor xor_1 (xor_1_out, A, B);
  and and_1 (and_1_out, cIn, xor_1_out);
  and and_2 (and_2_out, A, B);
  xor xor_2 (S, xor_1_out, cIn);
  or or_1 (cOut, and_1_out, and_2_out);
endmodule
