// Digital circuit Subtrator1bit.dig as structural Verilog
module Subtrator1bit (
  input  A,
  input  B,
  input  cIn,
  output S,
  output cOut
);

  wire and_1_out, and_2_out, and_3_out, not_1_out, not_2_out;

  not not_1 (not_1_out, A);
  not not_2 (not_2_out, A);
  xor xor_1 (S, B, cIn, A);
  and and_1 (and_1_out, not_1_out, B);
  and and_2 (and_2_out, not_2_out, cIn);
  and and_3 (and_3_out, B, cIn);
  or or_1 (cOut, and_1_out, and_2_out, and_3_out);
endmodule
