// Digital circuit Subtrator8bits.dig as structural Verilog
module Subtrator8bits (
  input  [7:0] B,
  input  [7:0] A,
  output [7:0] S,
  output cOut
);

  wire subtrator1bit_1_cout, subtrator1bit_2_cout, subtrator1bit_3_cout, subtrator1bit_4_cout,
       subtrator1bit_5_cout, subtrator1bit_6_cout, subtrator1bit_7_cout;

  Subtrator1bit subtrator1bit_1 (.A(A[0]), .B(B[0]), .cIn(1'b0), .S(S[0]), .cOut(subtrator1bit_1_cout));
  Subtrator1bit subtrator1bit_2 (.A(A[1]), .B(B[1]), .cIn(subtrator1bit_1_cout), .S(S[1]), .cOut(subtrator1bit_2_cout));
  Subtrator1bit subtrator1bit_3 (.A(A[2]), .B(B[2]), .cIn(subtrator1bit_2_cout), .S(S[2]), .cOut(subtrator1bit_3_cout));
  Subtrator1bit subtrator1bit_4 (.A(A[3]), .B(B[3]), .cIn(subtrator1bit_3_cout), .S(S[3]), .cOut(subtrator1bit_4_cout));
  Subtrator1bit subtrator1bit_5 (.A(A[4]), .B(B[4]), .cIn(subtrator1bit_4_cout), .S(S[4]), .cOut(subtrator1bit_5_cout));
  Subtrator1bit subtrator1bit_6 (.A(A[5]), .B(B[5]), .cIn(subtrator1bit_5_cout), .S(S[5]), .cOut(subtrator1bit_6_cout));
  Subtrator1bit subtrator1bit_7 (.A(A[6]), .B(B[6]), .cIn(subtrator1bit_6_cout), .S(S[6]), .cOut(subtrator1bit_7_cout));
  Subtrator1bit subtrator1bit_8 (.A(A[7]), .B(B[7]), .cIn(subtrator1bit_7_cout), .S(S[7]), .cOut(cOut));

  // Other names for the same wires on the sheet: A1 = A[0]; A2 = A[1]; A3 = A[2]; A4 = A[3]; A5 = A[4]; A6 = A[5];
  //   A7 = A[6]; A8 = A[7]; B1 = B[0]; B2 = B[1]; B3 = B[2]; B4 = B[3]; B5 = B[4]; B6 = B[5]; B7 = B[6]; B8 = B[7]
endmodule
