// Digital circuit XOR8bits.dig as structural Verilog
module XOR8bits (
  input  [7:0] A,
  input  [7:0] B,
  output [7:0] S
);

  xor xor_1 (S[0], A[0], B[0]);
  xor xor_2 (S[1], A[1], B[1]);
  xor xor_3 (S[2], A[2], B[2]);
  xor xor_4 (S[3], A[3], B[3]);
  xor xor_5 (S[4], A[4], B[4]);
  xor xor_6 (S[5], A[5], B[5]);
  xor xor_7 (S[6], A[6], B[6]);
  xor xor_8 (S[7], A[7], B[7]);

  // Other names for the same wires on the sheet: A1 = A[0]; A2 = A[1]; A3 = A[2]; A4 = A[3]; A5 = A[4]; A6 = A[5];
  //   A7 = A[6]; A8 = A[7]; B1 = B[0]; B2 = B[1]; B3 = B[2]; B4 = B[3]; B5 = B[4]; B6 = B[5]; B7 = B[6]; B8 = B[7];
  //   S1 = S[0]; S2 = S[1]; S3 = S[2]; S4 = S[3]; S5 = S[4]; S6 = S[5]; S7 = S[6]; S8 = S[7]
endmodule
