// Digital circuit divisorSimples.dig as structural Verilog
module divisorSimples (
  input  [7:0] A,
  input  [7:0] B,
  output [7:0] S,
  output cOut
);

  wire subtrator8bits_1_cout;
  wire [7:0] subtrator8bits_1_s;

  Subtrator8bits subtrator8bits_1 (.B(B), .A(A), .S(subtrator8bits_1_s), .cOut(subtrator8bits_1_cout));
  Multiplexer #(.Bits(8)) multiplexer_1 (.sel(subtrator8bits_1_cout), .in_0(subtrator8bits_1_s), .in_1(A), .out(S));
  not not_1 (cOut, subtrator8bits_1_cout);
endmodule
